// Digital circuit RV5-PCU.dig as structural Verilog
module RV5_PCU (
  input  [31:0] IMM_32,
  input  CLK,
  input  IS_BRANCH,
  input  IS_JAL,
  input  IS_JALR,
  input  COND_MET,
  input  [31:0] ALU_OUT,
  input  IS_ECALL,
  input  [31:0] MTVEC,
  input  [31:0] MEPC,
  input  IS_MRET,
  output [31:0] PC
);

  wire and_1_out, or_1_out;
  wire [1:0] priorityencoder_1_num;
  wire [29:0] multiplexer_1_out, multiplexer_2_out, PC_Incr_s;

  Register #(.Bits(30)) PC_w (.D(multiplexer_2_out), .C(CLK), .en(1'b1), .Q(PC[31:2]));
  and and_1 (and_1_out, IS_BRANCH, COND_MET);
  or or_1 (or_1_out, IS_JAL, and_1_out);
  Multiplexer #(.Bits(30)) multiplexer_1 (.sel(or_1_out), .in_0(30'h1), .in_1(IMM_32[31:2]), .out(multiplexer_1_out));
  Add #(.Bits(30)) PC_Incr (.a(PC[31:2]), .b(multiplexer_1_out), .c_i(1'b0), .s(PC_Incr_s));  // open: c_o
  PriorityEncoder #(.Selector_Bits(2)) priorityencoder_1 (
    .in0(1'b0), .in1(IS_JALR), .in2(IS_ECALL), .in3(IS_MRET), .num(priorityencoder_1_num));  // open: any
  Multiplexer #(.Selector_Bits(2), .Bits(30)) multiplexer_2 (
    .sel(priorityencoder_1_num), .in_0(PC_Incr_s), .in_1(ALU_OUT[31:2]), .in_2(MTVEC[31:2]),
    .in_3(MEPC[31:2]), .out(multiplexer_2_out));

  assign PC[1:0] = 2'b00;

  // Other names for the same wires on the sheet: sgn_ext_imm32[31:0] = IMM_32

  // Notes on the sheet:
  //   PCU(Program Control Unit)
  //   IMM_32 should probably be replaced 
  //   with sgn-ext-imm32 from RV5-IMM
  //   PC = PC + 4, or PC = PC += SBimm32
  //   or PC = ALU out or PC += sgn_ext-imm32
  //   for FMT U, and UJ
  //   /30
endmodule
