// Digital circuit RV5-CONTROL-LOGIC.dig as structural Verilog
module RV5_CONTROL_LOGIC (
  input  [6:0] opcode,
  input  [2:0] funct3,
  input  [11:0] funct12,
  output [4:0] inst_format,
  output reg_wen,
  output mem_wen,
  output mem_ren,
  output mem_b,
  output mem_h,
  output ld_signext,
  output [1:0] alu_asel,
  output alu_bsel,
  output [3:0] alu_op,
  output branch_sel,
  output jal_sel,
  output jalr_sel,
  output [1:0] wb_sel
);

  wire and_4_out, and_5_out, and_6_out, is_alu, is_auipc, is_mem, is_op, is_op_imm, or_8_out, or_10_out;

  RV5_OPCODE_DECODE rv5_opcode_decode_1 (
    .opcode(opcode), .is_load(mem_ren), .is_opimm(is_op_imm), .is_auipc(is_auipc), .is_store(inst_format[1]),
    .is_op(is_op), .is_lui(alu_asel[1]), .is_branch(branch_sel), .is_jalr(jalr_sel), .is_jal(inst_format[4]));  // open: is_system
  or or_1 (reg_wen, mem_ren, is_op_imm, is_auipc, is_op, alu_asel[1], jalr_sel, inst_format[4]);
  or or_2 (wb_sel[0], jalr_sel, inst_format[4]);
  or or_3 (alu_asel[0], is_auipc, inst_format[4]);
  or or_4 (alu_bsel, mem_ren, is_op_imm, is_auipc, inst_format[1], alu_asel[1], jalr_sel, inst_format[4]);
  or or_5 (inst_format[0], mem_ren, is_op_imm, jalr_sel);
  or or_6 (inst_format[3], alu_asel[1], is_auipc);
  or or_7 (is_mem, mem_ren, inst_format[1]);
  and and_1 (mem_b, is_mem, ~funct3[1], ~funct3[0]);  // And
  and and_2 (mem_h, is_mem, ~funct3[1], funct3[0]);  // And
  and and_3 (ld_signext, mem_ren, ~funct3[2]);  // And
  or or_8 (or_8_out, is_op_imm, is_op, branch_sel);
  or or_9 (is_alu, is_op_imm, is_op);
  and and_4 (and_4_out, is_op, funct12[10], ~funct3[2], ~funct3[1], ~funct3[0]);  // And
  and and_5 (and_5_out, is_alu, ~funct3[2], ~funct3[1], funct3[0]);  // And
  and and_6 (and_6_out, is_alu, funct12[10], funct3[2], ~funct3[1], funct3[0]);  // And
  Multiplexer #(.Bits(3)) multiplexer_1 (.sel(or_8_out), .in_0(3'b000), .in_1(funct3), .out(alu_op[2:0]));
  or or_10 (or_10_out, and_4_out, and_5_out, and_6_out);
  or or_11 (alu_op[3], branch_sel, or_10_out);

  assign inst_format[2] = branch_sel;
  assign jal_sel = inst_format[4];
  assign mem_wen = inst_format[1];
  assign wb_sel[1] = mem_ren;

  // Other names for the same wires on the sheet: f3_0 = funct3[0]; f3_1 = funct3[1]; f3_2 = funct3[2];
  //   inst30 = funct12[10]; is_branch = branch_sel; is_jal = inst_format[4]; is_jalr = jalr_sel; is_load = mem_ren;
  //   is_lui = alu_asel[1]; is_store = inst_format[1]

  // Notes on the sheet:
  //   RV5-CONTROL-LOGIC
  //   Decode
  //   Register writing
  //   Every instruction writes rd except STORE and BRANCH.
  //   wb-sel: 0 = ALU, 1 = PC+4, 2 = memory
  //   ALU operands
  //   alu-asel: 0 = rs1, 1 = PC, 2 = zero
  //   alu-bsel: 0 = rs2, 1 = imm
  //   inst-format[4:0]: one wire per format, J U B S I
  //   Branch and jump
  //   We just pass along the instruction class.
  //   Memory
  //   funct3[1:0] is the size: 00 = byte, 01 = half, 10 = word
  //   funct3[2] = 1 zero-extends the load (LBU, LHU)
  //   ALU operation
  //   alu-op[2:0] is funct3 for OP, OP-IMM and BRANCH, else 0 (add)
  //   alu-op[3] is set for SUB, SLL, SRA and all branches
  //   uses funct3
  //   SUB
  //   SLL
  //   SRA
endmodule
