// Digital circuit RV5-PCU.dig as structural Verilog
module RV5_PCU (
  input  jalr_sel,
  input  clk,
  input  [31:0] npc,
  input  [31:0] alu_out,
  input  br_jmp,
  input  [31:0] imm_signext,
  output [31:0] pc,
  output [31:0] npc_2
);

  wire [31:0] multiplexer_1_out, PC_Incr_s;

  Multiplexer #(.Bits(32)) multiplexer_1 (.sel(br_jmp), .in_0(32'h4), .in_1(imm_signext), .out(multiplexer_1_out));
  Add #(.Bits(32)) PC_Incr (.a(pc), .b(multiplexer_1_out), .c_i(1'b0), .s(PC_Incr_s));  // open: c_o
  Multiplexer #(.Bits(32)) multiplexer_2 (.sel(jalr_sel), .in_0(PC_Incr_s), .in_1({alu_out[31:1], 1'b0}), .out(npc_2));
  D_FF #(.Bits(32)) u_PC (.D(npc), .C(clk), .Q(pc));  // open: nQ

  // Other names for the same wires on the sheet: jalr_dest[31:1] = alu_out[31:1]; immed[31:0] = imm_signext;
  //   is_jalr = jalr_sel; npc_t[31:0] = npc_2

  // Notes on the sheet:
  //   RV5-PCU
  //   debug system stuff - ignore
  //   you can pretend it goes
  //   straight across.
  //   /31
endmodule
